# Fritzing sketch tictactino (saved by Fritzing 0.7.12b)
breadboards: 1

parts:
  Arduino1 = Arduino
  S1 = Pushbutton [package="[THT]"]
  S2 = Pushbutton [package="[THT]"]
  R1 = Resistor [tolerance=±5% resistance=10k package=THT]
  R2 = Resistor [tolerance=±5% resistance=10k package=THT]

nets:
  N1: Arduino1.D3, S2.Pin_3, S2.Pin_4, R2.Pin_1
  N2: Arduino1.D2, S1.Pin_3, S1.Pin_4, R1.Pin_1
  N3: Arduino1.+5V, S1.Pin_1, S1.Pin_2, S2.Pin_1, S2.Pin_2
  N4: Arduino1.GND, R1.Pin_0, R2.Pin_0
